# Fritzing sketch CordChord_perfboard (saved by Fritzing 0.9.3b)
perfboards: 1

parts:
  TrillCraft = Trill Craft
  J3 = female pin header, 2 pins [form="♀ (female)"]  # not connected
  J4 = female pin header, 2 pins [form="♀ (female)"]  # not connected
  J5 = female pin header, 8 pins [form="♀ (female)"]
  J6 = female pin header, 2 pins [form="♀ (female)"]
  J7 = female pin header, 2 pins [form="♀ (female)"]
  J8 = female pin header, 2 pins [form="♀ (female)"]
  R1 = Resistor [tolerance=±5% resistance=330k package="2512 [SMD]"]  # not connected
  R2 = Resistor [tolerance=±5% resistance=330k package="2512 [SMD]"]  # not connected
  R3 = Resistor [tolerance=±5% resistance=330k package="2512 [SMD]"]  # not connected
  R4 = Resistor [tolerance=±5% resistance=330k package="2512 [SMD]"]  # not connected
  R5 = Resistor [tolerance=±5% resistance=330k package="2512 [SMD]"]  # not connected
  R6 = Resistor [tolerance=±5% resistance=330k package="2512 [SMD]"]  # not connected
  R7 = Resistor [tolerance=±5% resistance=330k package="2512 [SMD]"]  # not connected
  R8 = Resistor [tolerance=±5% resistance=330k package="2512 [SMD]"]  # not connected
  R9 = Resistor [tolerance=±5% resistance=680 package="2512 [SMD]"]  # not connected
  R10 = Resistor [tolerance=±5% resistance=680 package="2512 [SMD]"]  # not connected
  R11 = Resistor [tolerance=±5% resistance=680 package="2512 [SMD]"]  # not connected
  R12 = Resistor [tolerance=±5% resistance=680 package="2512 [SMD]"]  # not connected
  R13 = Resistor [tolerance=±5% resistance=680 package="2512 [SMD]"]  # not connected
  R14 = Resistor [tolerance=±5% resistance=680 package="2512 [SMD]"]  # not connected
  R15 = Resistor [tolerance=±5% resistance=680 package="2512 [SMD]"]  # not connected
  R16 = Resistor [tolerance=±5% resistance=680 package="2512 [SMD]"]  # not connected
  J9 = female pin header, 8 pins [form="♀ (female)"]  # not connected
  J10 = female pin header, 8 pins [form="♀ (female)"]  # not connected
  J11 = female pin header, 8 pins [form="♀ (female)"]  # not connected
  J12 = female pin header, 8 pins [form="♀ (female)"]  # not connected
  J13 = female pin header, 4 pins [form="♀ (female)"]
  J14 = female pin header, 2 pins [form="♀ (female)"]
  Bela1 = Bela  # not connected
  J15 = female pin header, 9 pins [form="♀ (female)"]
  J16 = female pin header, 9 pins [form="♀ (female)"]

nets:
  N1: TrillCraft.SCL, J6.pin2, J13.pin3
  N2: TrillCraft.SDA, J6.pin1, J13.pin4
  N3: TrillCraft.VCC, J7.pin1, J13.pin2
  N4: TrillCraft.GND, J7.pin2, J13.pin1
  N5: TrillCraft.0, J15.pin9
  N6: TrillCraft.1, J15.pin8
  N7: TrillCraft.2, J15.pin7
  N8: TrillCraft.3, J15.pin6
  N9: TrillCraft.4, J15.pin5
  N10: TrillCraft.5, J15.pin4
  N11: TrillCraft.6, J15.pin3
  N12: TrillCraft.7, J14.pin1, J15.pin2
  N13: TrillCraft.8, J14.pin2, J15.pin1
  N14: TrillCraft.21, J16.pin1
  N15: TrillCraft.22, J16.pin2
  N16: TrillCraft.23, J16.pin3
  N17: TrillCraft.24, J16.pin4
  N18: TrillCraft.25, J16.pin5
  N19: TrillCraft.26, J16.pin6
  N20: TrillCraft.27, J16.pin7
  N21: TrillCraft.28, J16.pin8
  N22: TrillCraft.29, J16.pin9
  N23: J5.pin8, J8.pin2

custom parts:
  Trill Craft: A 30-channel breakout board for building touch interfaces out of any conductive material, by Bela.io
  Bela: A Fritzing part for Bela
